// Logisim project index.circ as structural Verilog: 16 circuits, main circuit main
module main (
  input  [4:0] A,
  input  [4:0] B,
  input  in_3,
  input  in_4
);

  wire display_carry_1_a, display_carry_1_b, display_carry_1_c, display_carry_1_d, display_carry_1_e,
       display_carry_1_f, display_carry_1_g, display_carry_2_a, display_carry_2_b, display_carry_2_c,
       display_carry_2_d, display_carry_2_e, display_carry_2_f, display_carry_2_g, display_carry_3_a,
       display_carry_3_b, display_carry_3_c, display_carry_3_d, display_carry_3_e, display_carry_3_f,
       display_carry_3_g, n5_bitadder_1_carry, n5_bitadder_1_s0, n5_bitadder_1_s1, n5_bitadder_1_s2,
       n5_bitadder_1_s3, n5_bitadder_1_s4, n7_segment_display_1_a_2, n7_segment_display_1_b_2,
       n7_segment_display_1_c_2, n7_segment_display_1_d_2, n7_segment_display_1_e_2,
       n7_segment_display_1_f_2, n7_segment_display_1_five, n7_segment_display_1_four,
       n7_segment_display_1_g, n7_segment_display_1_one, n7_segment_display_1_six,
       n7_segment_display_1_three, n7_segment_display_1_two, n7_segment_display_4_a_2,
       n7_segment_display_4_b_2, n7_segment_display_4_c_2, n7_segment_display_4_d_2,
       n7_segment_display_4_e_2, n7_segment_display_4_f_2, n7_segment_display_4_five,
       n7_segment_display_4_four, n7_segment_display_4_g, n7_segment_display_4_one, n7_segment_display_4_six,
       n7_segment_display_4_three, n7_segment_display_4_two, n7_segment_display_7_a_2,
       n7_segment_display_7_b_2, n7_segment_display_7_c_2, n7_segment_display_7_d_2,
       n7_segment_display_7_e_2, n7_segment_display_7_f_2, n7_segment_display_7_five,
       n7_segment_display_7_four, n7_segment_display_7_g, n7_segment_display_7_one, n7_segment_display_7_six,
       n7_segment_display_7_three, n7_segment_display_7_two;
  wire [3:0] n7_segment_display_1_hex_0, n7_segment_display_1_hex_1, n7_segment_display_4_hex_0,
       n7_segment_display_4_hex_1, n7_segment_display_7_hex_0, n7_segment_display_7_hex_1;

  Hex_Digit_Display hex_digit_display_1 (.value(n7_segment_display_1_hex_1));  // open: dp
  Hex_Digit_Display hex_digit_display_2 (.value(n7_segment_display_1_hex_0));  // open: dp
  Display_Carry display_carry_1 (
    .A(display_carry_1_a), .B(display_carry_1_b), .C(display_carry_1_c), .D(display_carry_1_d),
    .E(display_carry_1_e), .F(display_carry_1_f), .G(display_carry_1_g), .Six(n7_segment_display_1_six),
    .Five(n7_segment_display_1_five), .Four(n7_segment_display_1_four), .Three(n7_segment_display_1_three),
    .Two(n7_segment_display_1_two), .One(n7_segment_display_1_one));
  _7_Segment_Display u_7_segment_display_1 (
    .Enable(in_4), .One(n7_segment_display_1_one), .Two(n7_segment_display_1_two),
    .Three(n7_segment_display_1_three), .Four(n7_segment_display_1_four), .Five(n7_segment_display_1_five),
    .Six(n7_segment_display_1_six), .A_2(n7_segment_display_1_a_2), .B_2(n7_segment_display_1_b_2),
    .D_2(n7_segment_display_1_d_2), .E_2(n7_segment_display_1_e_2), .F_2(n7_segment_display_1_f_2),
    .G(n7_segment_display_1_g), .F(1'b0), .E(A[4]), .D(A[3]), .C(A[2]), .B(A[1]), .A(A[0]),
    .C_2(n7_segment_display_1_c_2), .Hex_0(n7_segment_display_1_hex_0), .Hex_1(n7_segment_display_1_hex_1));
  _7_Segment_Display_part u_7_segment_display_2 (
    .g(display_carry_1_g), .f(display_carry_1_f), .a(display_carry_1_a), .b(display_carry_1_b),
    .e(display_carry_1_e), .d(display_carry_1_d), .c(display_carry_1_c));  // open: dp
  _7_Segment_Display_part u_7_segment_display_3 (
    .g(n7_segment_display_1_g), .f(n7_segment_display_1_f_2), .a(n7_segment_display_1_a_2),
    .b(n7_segment_display_1_b_2), .e(n7_segment_display_1_e_2), .d(n7_segment_display_1_d_2),
    .c(n7_segment_display_1_c_2));  // open: dp
  Hex_Digit_Display hex_digit_display_3 (.value(n7_segment_display_4_hex_1));  // open: dp
  Hex_Digit_Display hex_digit_display_4 (.value(n7_segment_display_4_hex_0));  // open: dp
  Display_Carry display_carry_2 (
    .A(display_carry_2_a), .B(display_carry_2_b), .C(display_carry_2_c), .D(display_carry_2_d),
    .E(display_carry_2_e), .F(display_carry_2_f), .G(display_carry_2_g), .Six(n7_segment_display_4_six),
    .Five(n7_segment_display_4_five), .Four(n7_segment_display_4_four), .Three(n7_segment_display_4_three),
    .Two(n7_segment_display_4_two), .One(n7_segment_display_4_one));
  _7_Segment_Display u_7_segment_display_4 (
    .Enable(in_4), .One(n7_segment_display_4_one), .Two(n7_segment_display_4_two),
    .Three(n7_segment_display_4_three), .Four(n7_segment_display_4_four), .Five(n7_segment_display_4_five),
    .Six(n7_segment_display_4_six), .A_2(n7_segment_display_4_a_2), .B_2(n7_segment_display_4_b_2),
    .D_2(n7_segment_display_4_d_2), .E_2(n7_segment_display_4_e_2), .F_2(n7_segment_display_4_f_2),
    .G(n7_segment_display_4_g), .F(1'b0), .E(B[4]), .D(B[3]), .C(B[2]), .B(B[1]), .A(B[0]),
    .C_2(n7_segment_display_4_c_2), .Hex_0(n7_segment_display_4_hex_0), .Hex_1(n7_segment_display_4_hex_1));
  _7_Segment_Display_part u_7_segment_display_5 (
    .g(display_carry_2_g), .f(display_carry_2_f), .a(display_carry_2_a), .b(display_carry_2_b),
    .e(display_carry_2_e), .d(display_carry_2_d), .c(display_carry_2_c));  // open: dp
  _7_Segment_Display_part u_7_segment_display_6 (
    .g(n7_segment_display_4_g), .f(n7_segment_display_4_f_2), .a(n7_segment_display_4_a_2),
    .b(n7_segment_display_4_b_2), .e(n7_segment_display_4_e_2), .d(n7_segment_display_4_d_2),
    .c(n7_segment_display_4_c_2));  // open: dp
  Hex_Digit_Display hex_digit_display_5 (.value(n7_segment_display_7_hex_1));  // open: dp
  Hex_Digit_Display hex_digit_display_6 (.value(n7_segment_display_7_hex_0));  // open: dp
  _5_bitAdder u_5_bitadder_1 (
    .carry(n5_bitadder_1_carry), .Cin(in_3), .B4(B[4]), .A4(A[4]), .B3(B[3]), .A3(A[3]), .B2(B[2]),
    .A2(A[2]), .B1(B[1]), .A1(A[1]), .B0(B[0]), .A0(A[0]), .S4(n5_bitadder_1_s4), .S3(n5_bitadder_1_s3),
    .S2(n5_bitadder_1_s2), .S1(n5_bitadder_1_s1), .S0(n5_bitadder_1_s0));
  Display_Carry display_carry_3 (
    .A(display_carry_3_a), .B(display_carry_3_b), .C(display_carry_3_c), .D(display_carry_3_d),
    .E(display_carry_3_e), .F(display_carry_3_f), .G(display_carry_3_g), .Six(n7_segment_display_7_six),
    .Five(n7_segment_display_7_five), .Four(n7_segment_display_7_four), .Three(n7_segment_display_7_three),
    .Two(n7_segment_display_7_two), .One(n7_segment_display_7_one));
  _7_Segment_Display u_7_segment_display_7 (
    .Enable(in_4), .One(n7_segment_display_7_one), .Two(n7_segment_display_7_two),
    .Three(n7_segment_display_7_three), .Four(n7_segment_display_7_four), .Five(n7_segment_display_7_five),
    .Six(n7_segment_display_7_six), .A_2(n7_segment_display_7_a_2), .B_2(n7_segment_display_7_b_2),
    .D_2(n7_segment_display_7_d_2), .E_2(n7_segment_display_7_e_2), .F_2(n7_segment_display_7_f_2),
    .G(n7_segment_display_7_g), .F(n5_bitadder_1_carry), .E(n5_bitadder_1_s4), .D(n5_bitadder_1_s3),
    .C(n5_bitadder_1_s2), .B(n5_bitadder_1_s1), .A(n5_bitadder_1_s0), .C_2(n7_segment_display_7_c_2),
    .Hex_0(n7_segment_display_7_hex_0), .Hex_1(n7_segment_display_7_hex_1));
  _7_Segment_Display_part u_7_segment_display_8 (
    .g(display_carry_3_g), .f(display_carry_3_f), .a(display_carry_3_a), .b(display_carry_3_b),
    .e(display_carry_3_e), .d(display_carry_3_d), .c(display_carry_3_c));  // open: dp
  _7_Segment_Display_part u_7_segment_display_9 (
    .g(n7_segment_display_7_g), .f(n7_segment_display_7_f_2), .a(n7_segment_display_7_a_2),
    .b(n7_segment_display_7_b_2), .e(n7_segment_display_7_e_2), .d(n7_segment_display_7_d_2),
    .c(n7_segment_display_7_c_2));  // open: dp

  // Notes on the sheet:
  //   Hex/Dec Switch
  //   +
  //   =
endmodule

module HA (
  input  A,
  input  B,
  output sum,
  output carry
);

  xor xor_1 (sum, A, B);
  and and_1 (carry, A, B);
endmodule

module FullAdder (
  input  Cin,
  input  A,
  input  B,
  output Sum,
  output Cout
);

  wire ha_1_carry, ha_1_sum, ha_2_carry;

  HA ha_1 (.A(A), .B(B), .sum(ha_1_sum), .carry(ha_1_carry));
  HA ha_2 (.A(Cin), .B(ha_1_sum), .sum(Sum), .carry(ha_2_carry));
  xor xor_1 (Cout, ha_2_carry, ha_1_carry);
endmodule

module _5_bitAdder (
  input  B0,
  input  A0,
  input  B1,
  input  A1,
  input  B2,
  input  A2,
  input  B3,
  input  A3,
  input  B4,
  input  A4,
  input  Cin,
  output carry,
  output S3,
  output S2,
  output S1,
  output S0,
  output S4
);

  wire fulladder_2_cout, fulladder_3_cout, fulladder_4_cout, fulladder_5_cout;

  FullAdder fulladder_1 (.Cin(fulladder_2_cout), .A(A4), .B(B4), .Sum(S4), .Cout(carry));
  FullAdder fulladder_2 (.Cin(fulladder_3_cout), .A(A3), .B(B3), .Sum(S3), .Cout(fulladder_2_cout));
  FullAdder fulladder_3 (.Cin(fulladder_4_cout), .A(A2), .B(B2), .Sum(S2), .Cout(fulladder_3_cout));
  FullAdder fulladder_4 (.Cin(fulladder_5_cout), .A(A1), .B(B1), .Sum(S1), .Cout(fulladder_4_cout));
  FullAdder fulladder_5 (.Cin(Cin), .A(A0), .B(B0), .Sum(S0), .Cout(fulladder_5_cout));
endmodule

module _6x64_Decoder (
  input  S0,
  input  S1,
  input  S2,
  input  S3,
  input  S4,
  input  S5,
  input  Enable,
  output Out_0,
  output Out_1,
  output Out_2,
  output Out_3,
  output Out_4,
  output Out_5,
  output Out_6,
  output Out_7,
  output Out_8,
  output Out_9,
  output Out_10,
  output Out_11,
  output Out_12,
  output Out_13,
  output Out_14,
  output Out_15,
  output Out_16,
  output Out_17,
  output Out_18,
  output Out_19,
  output Out_20,
  output Out_21,
  output Out_22,
  output Out_23,
  output Out_24,
  output Out_25,
  output Out_26,
  output Out_27,
  output Out_28,
  output Out_29,
  output Out_30,
  output Out_31,
  output Out_32,
  output Out_33,
  output Out_34,
  output Out_35,
  output Out_36,
  output Out_37,
  output Out_38,
  output Out_39,
  output Out_40,
  output Out_41,
  output Out_42,
  output Out_43,
  output Out_44,
  output Out_45,
  output Out_46,
  output Out_47,
  output Out_48,
  output Out_49,
  output Out_50,
  output Out_51,
  output Out_52,
  output Out_53,
  output Out_54,
  output Out_55,
  output Out_56,
  output Out_57,
  output Out_58,
  output Out_59,
  output Out_60,
  output Out_61,
  output Out_62,
  output Out_63
);

  wire and_1_out, and_2_out, and_3_out, and_4_out, decoder_1_out0, decoder_1_out1, decoder_1_out2,
       decoder_1_out3;

  Decoder #(.select(2)) decoder_1 (
    .out0(decoder_1_out0), .out1(decoder_1_out1), .out2(decoder_1_out2), .out3(decoder_1_out3),
    .sel({S5, S4}), .en(Enable));
  and and_1 (and_1_out, decoder_1_out0, Enable);
  and and_2 (and_2_out, decoder_1_out1, Enable);
  and and_3 (and_3_out, Enable, decoder_1_out2);
  and and_4 (and_4_out, decoder_1_out3, Enable);
  Decoder #(.select(4), .disabled(0)) decoder_2 (
    .out0(Out_0), .out1(Out_1), .out2(Out_2), .out3(Out_3), .out4(Out_4), .out5(Out_5), .out6(Out_6),
    .out7(Out_7), .out8(Out_8), .out9(Out_9), .out10(Out_10), .out11(Out_11), .out12(Out_12), .out13(Out_13),
    .out14(Out_14), .out15(Out_15), .sel({S3, S2, S1, S0}), .en(and_1_out));
  Decoder #(.select(4), .disabled(0)) decoder_3 (
    .out0(Out_16), .out1(Out_17), .out2(Out_18), .out3(Out_19), .out4(Out_20), .out5(Out_21), .out6(Out_22),
    .out7(Out_23), .out8(Out_24), .out9(Out_25), .out10(Out_26), .out11(Out_27), .out12(Out_28),
    .out13(Out_29), .out14(Out_30), .out15(Out_31), .sel({S3, S2, S1, S0}), .en(and_2_out));
  Decoder #(.select(4), .disabled(0)) decoder_4 (
    .out0(Out_32), .out1(Out_33), .out2(Out_34), .out3(Out_35), .out4(Out_36), .out5(Out_37), .out6(Out_38),
    .out7(Out_39), .out8(Out_40), .out9(Out_41), .out10(Out_42), .out11(Out_43), .out12(Out_44),
    .out13(Out_45), .out14(Out_46), .out15(Out_47), .sel({S3, S2, S1, S0}), .en(and_3_out));
  Decoder #(.select(4), .disabled(0)) decoder_5 (
    .out0(Out_48), .out1(Out_49), .out2(Out_50), .out3(Out_51), .out4(Out_52), .out5(Out_53), .out6(Out_54),
    .out7(Out_55), .out8(Out_56), .out9(Out_57), .out10(Out_58), .out11(Out_59), .out12(Out_60),
    .out13(Out_61), .out14(Out_62), .out15(Out_63), .sel({S3, S2, S1, S0}), .en(and_4_out));
endmodule

module _7_Segment_Display (
  input  F,
  input  E,
  input  D,
  input  C,
  input  B,
  input  A,
  input  Enable,
  output One,
  output Two,
  output Three,
  output Four,
  output Five,
  output Six,
  output A_2,
  output B_2,
  output C_2,
  output D_2,
  output E_2,
  output F_2,
  output G,
  output [3:0] Hex_1,
  output [3:0] Hex_0
);

  wire not_1_out;

  Display_Hex display_hex_1 (
    ._32(F), ._16(E), ._8(D), ._4(C), ._2(B), ._1(A), .out_9(Hex_0), .out_8(Hex_1), .switsh(not_1_out));
  not not_1 (not_1_out, Enable);
  Get_Segment_carry get_segment_carry_1 (
    .in_1(Enable), .S5(F), .S4(E), .S3(D), .S2(C), .S1(B), .S0(A), .Six(Six), .Five(Five), .Four(Four),
    .Three(Three), .Two(Two), .One(One));
  Segment___A segment_a_1 (.A(A_2), .S3(D), .S2(C), .S1(B), .S0(A), .S5(F), .S4(E), .in_1(Enable));
  Segment___B segment_b_1 (.in_1(Enable), .S5(F), .S4(E), .S3(D), .S2(C), .S1(B), .S0(A), .B(B_2));
  Segment___C segment_c_1 (.in_1(Enable), .S5(F), .S4(E), .S3(D), .S2(C), .S1(B), .S0(A), .C(C_2));
  Segment___D segment_d_1 (.in_1(Enable), .S5(F), .S4(E), .S3(D), .S2(C), .S1(B), .S0(A), .D(D_2));
  Segment___E segment_e_1 (.in_1(Enable), .S5(F), .S4(E), .S3(D), .S2(C), .S1(B), .S0(A), .D(E_2));
  Segment___F segment_f_1 (.in_1(Enable), .S5(F), .S4(E), .S3(D), .S2(C), .S1(B), .S0(A), .F(F_2));
  Segment___G segment_g_1 (.in_1(Enable), .S5(F), .S4(E), .S3(D), .S2(C), .S1(B), .S0(A), .G(G));
endmodule

module Segment___A (
  input  in_1,
  input  S5,
  input  S4,
  input  S3,
  input  S2,
  input  S1,
  input  S0,
  output A
);

  wire n6x64_decoder_1_out_0, n6x64_decoder_1_out_1, n6x64_decoder_1_out_2, n6x64_decoder_1_out_3,
       n6x64_decoder_1_out_4, n6x64_decoder_1_out_5, n6x64_decoder_1_out_6, n6x64_decoder_1_out_7,
       n6x64_decoder_1_out_8, n6x64_decoder_1_out_9, n6x64_decoder_1_out_10, n6x64_decoder_1_out_11,
       n6x64_decoder_1_out_12, n6x64_decoder_1_out_13, n6x64_decoder_1_out_14, n6x64_decoder_1_out_15,
       n6x64_decoder_1_out_16, n6x64_decoder_1_out_17, n6x64_decoder_1_out_18, n6x64_decoder_1_out_19,
       n6x64_decoder_1_out_20, n6x64_decoder_1_out_21, n6x64_decoder_1_out_22, n6x64_decoder_1_out_23,
       n6x64_decoder_1_out_24, n6x64_decoder_1_out_25, n6x64_decoder_1_out_26, n6x64_decoder_1_out_27,
       n6x64_decoder_1_out_28, n6x64_decoder_1_out_29, n6x64_decoder_1_out_30, n6x64_decoder_1_out_31,
       n6x64_decoder_1_out_32, n6x64_decoder_1_out_33, n6x64_decoder_1_out_34, n6x64_decoder_1_out_35,
       n6x64_decoder_1_out_36, n6x64_decoder_1_out_37, n6x64_decoder_1_out_38, n6x64_decoder_1_out_39,
       n6x64_decoder_1_out_40, n6x64_decoder_1_out_41, n6x64_decoder_1_out_42, n6x64_decoder_1_out_43,
       n6x64_decoder_1_out_44, n6x64_decoder_1_out_45, n6x64_decoder_1_out_46, n6x64_decoder_1_out_47,
       n6x64_decoder_1_out_48, n6x64_decoder_1_out_49, n6x64_decoder_1_out_50, n6x64_decoder_1_out_51,
       n6x64_decoder_1_out_52, n6x64_decoder_1_out_53, n6x64_decoder_1_out_54, n6x64_decoder_1_out_55,
       n6x64_decoder_1_out_56, n6x64_decoder_1_out_57, n6x64_decoder_1_out_58, n6x64_decoder_1_out_59,
       n6x64_decoder_1_out_60, n6x64_decoder_1_out_62, n6x64_decoder_1_out_63, or_1_out, or_2_out, or_3_out,
       or_4_out, or_6_out, or_7_out, or_8_out;

  or or_1 (or_1_out, n6x64_decoder_1_out_63, n6x64_decoder_1_out_62, n6x64_decoder_1_out_60);
  or or_2 (or_2_out, n6x64_decoder_1_out_59, n6x64_decoder_1_out_58, n6x64_decoder_1_out_57, n6x64_decoder_1_out_56, n6x64_decoder_1_out_55, n6x64_decoder_1_out_53, n6x64_decoder_1_out_52, n6x64_decoder_1_out_50);
  or or_3 (or_3_out, n6x64_decoder_1_out_49, n6x64_decoder_1_out_48, n6x64_decoder_1_out_47, n6x64_decoder_1_out_46, n6x64_decoder_1_out_45, n6x64_decoder_1_out_43, n6x64_decoder_1_out_42, n6x64_decoder_1_out_40);
  _6x64_Decoder u_6x64_decoder_1 (
    .S0(S0), .S1(S1), .S2(S2), .S3(S3), .S4(S4), .S5(S5), .Out_0(n6x64_decoder_1_out_0),
    .Out_1(n6x64_decoder_1_out_1), .Out_2(n6x64_decoder_1_out_2), .Out_3(n6x64_decoder_1_out_3),
    .Out_4(n6x64_decoder_1_out_4), .Out_5(n6x64_decoder_1_out_5), .Out_6(n6x64_decoder_1_out_6),
    .Out_7(n6x64_decoder_1_out_7), .Out_8(n6x64_decoder_1_out_8), .Out_9(n6x64_decoder_1_out_9),
    .Out_10(n6x64_decoder_1_out_10), .Out_11(n6x64_decoder_1_out_11), .Out_12(n6x64_decoder_1_out_12),
    .Out_13(n6x64_decoder_1_out_13), .Out_14(n6x64_decoder_1_out_14), .Out_15(n6x64_decoder_1_out_15),
    .Out_16(n6x64_decoder_1_out_16), .Out_17(n6x64_decoder_1_out_17), .Out_18(n6x64_decoder_1_out_18),
    .Out_19(n6x64_decoder_1_out_19), .Out_20(n6x64_decoder_1_out_20), .Out_21(n6x64_decoder_1_out_21),
    .Out_22(n6x64_decoder_1_out_22), .Out_23(n6x64_decoder_1_out_23), .Out_24(n6x64_decoder_1_out_24),
    .Out_25(n6x64_decoder_1_out_25), .Out_26(n6x64_decoder_1_out_26), .Out_27(n6x64_decoder_1_out_27),
    .Out_28(n6x64_decoder_1_out_28), .Out_29(n6x64_decoder_1_out_29), .Out_30(n6x64_decoder_1_out_30),
    .Out_31(n6x64_decoder_1_out_31), .Out_32(n6x64_decoder_1_out_32), .Out_33(n6x64_decoder_1_out_33),
    .Out_34(n6x64_decoder_1_out_34), .Out_35(n6x64_decoder_1_out_35), .Out_36(n6x64_decoder_1_out_36),
    .Out_37(n6x64_decoder_1_out_37), .Out_38(n6x64_decoder_1_out_38), .Out_39(n6x64_decoder_1_out_39),
    .Out_40(n6x64_decoder_1_out_40), .Out_41(n6x64_decoder_1_out_41), .Out_42(n6x64_decoder_1_out_42),
    .Out_43(n6x64_decoder_1_out_43), .Out_44(n6x64_decoder_1_out_44), .Out_45(n6x64_decoder_1_out_45),
    .Out_46(n6x64_decoder_1_out_46), .Out_47(n6x64_decoder_1_out_47), .Enable(in_1),
    .Out_48(n6x64_decoder_1_out_48), .Out_49(n6x64_decoder_1_out_49), .Out_50(n6x64_decoder_1_out_50),
    .Out_51(n6x64_decoder_1_out_51), .Out_52(n6x64_decoder_1_out_52), .Out_53(n6x64_decoder_1_out_53),
    .Out_54(n6x64_decoder_1_out_54), .Out_55(n6x64_decoder_1_out_55), .Out_56(n6x64_decoder_1_out_56),
    .Out_57(n6x64_decoder_1_out_57), .Out_58(n6x64_decoder_1_out_58), .Out_59(n6x64_decoder_1_out_59),
    .Out_60(n6x64_decoder_1_out_60), .Out_62(n6x64_decoder_1_out_62), .Out_63(n6x64_decoder_1_out_63));  // open: Out_61
  or or_4 (or_4_out, n6x64_decoder_1_out_39, n6x64_decoder_1_out_38, n6x64_decoder_1_out_37, n6x64_decoder_1_out_36, n6x64_decoder_1_out_35, n6x64_decoder_1_out_33, n6x64_decoder_1_out_32, n6x64_decoder_1_out_30);
  or or_5 (A, or_2_out, or_3_out, or_4_out, or_1_out, or_6_out, or_7_out, or_8_out);
  or or_6 (or_6_out, n6x64_decoder_1_out_29, n6x64_decoder_1_out_28, n6x64_decoder_1_out_27, n6x64_decoder_1_out_26, n6x64_decoder_1_out_25, n6x64_decoder_1_out_23, n6x64_decoder_1_out_22, n6x64_decoder_1_out_20);
  or or_7 (or_7_out, n6x64_decoder_1_out_19, n6x64_decoder_1_out_18, n6x64_decoder_1_out_17, n6x64_decoder_1_out_16, n6x64_decoder_1_out_15, n6x64_decoder_1_out_13, n6x64_decoder_1_out_12, n6x64_decoder_1_out_10);
  or or_8 (or_8_out, n6x64_decoder_1_out_9, n6x64_decoder_1_out_8, n6x64_decoder_1_out_7, n6x64_decoder_1_out_6, n6x64_decoder_1_out_5, n6x64_decoder_1_out_3, n6x64_decoder_1_out_2, n6x64_decoder_1_out_0);
endmodule

module Segment___B (
  input  in_1,
  input  S5,
  input  S4,
  input  S3,
  input  S2,
  input  S1,
  input  S0,
  output B
);

  wire n6x64_decoder_1_out_0, n6x64_decoder_1_out_1, n6x64_decoder_1_out_2, n6x64_decoder_1_out_3,
       n6x64_decoder_1_out_4, n6x64_decoder_1_out_7, n6x64_decoder_1_out_8, n6x64_decoder_1_out_9,
       n6x64_decoder_1_out_10, n6x64_decoder_1_out_11, n6x64_decoder_1_out_12, n6x64_decoder_1_out_13,
       n6x64_decoder_1_out_14, n6x64_decoder_1_out_17, n6x64_decoder_1_out_18, n6x64_decoder_1_out_19,
       n6x64_decoder_1_out_20, n6x64_decoder_1_out_21, n6x64_decoder_1_out_22, n6x64_decoder_1_out_23,
       n6x64_decoder_1_out_24, n6x64_decoder_1_out_27, n6x64_decoder_1_out_28, n6x64_decoder_1_out_29,
       n6x64_decoder_1_out_30, n6x64_decoder_1_out_31, n6x64_decoder_1_out_32, n6x64_decoder_1_out_33,
       n6x64_decoder_1_out_34, n6x64_decoder_1_out_37, n6x64_decoder_1_out_38, n6x64_decoder_1_out_39,
       n6x64_decoder_1_out_40, n6x64_decoder_1_out_41, n6x64_decoder_1_out_42, n6x64_decoder_1_out_43,
       n6x64_decoder_1_out_44, n6x64_decoder_1_out_47, n6x64_decoder_1_out_48, n6x64_decoder_1_out_49,
       n6x64_decoder_1_out_50, n6x64_decoder_1_out_51, n6x64_decoder_1_out_52, n6x64_decoder_1_out_53,
       n6x64_decoder_1_out_54, n6x64_decoder_1_out_57, n6x64_decoder_1_out_58, n6x64_decoder_1_out_59,
       n6x64_decoder_1_out_60, n6x64_decoder_1_out_61, n6x64_decoder_1_out_62, n6x64_decoder_1_out_63,
       or_1_out, or_2_out, or_3_out, or_4_out, or_6_out, or_7_out, or_8_out;

  or or_1 (or_1_out, n6x64_decoder_1_out_63, n6x64_decoder_1_out_62, n6x64_decoder_1_out_61, n6x64_decoder_1_out_60);
  or or_2 (or_2_out, n6x64_decoder_1_out_59, n6x64_decoder_1_out_58, n6x64_decoder_1_out_57, n6x64_decoder_1_out_54, n6x64_decoder_1_out_53, n6x64_decoder_1_out_52, n6x64_decoder_1_out_51, n6x64_decoder_1_out_50);
  or or_3 (or_3_out, n6x64_decoder_1_out_49, n6x64_decoder_1_out_48, n6x64_decoder_1_out_47, n6x64_decoder_1_out_44, n6x64_decoder_1_out_43, n6x64_decoder_1_out_42, n6x64_decoder_1_out_41, n6x64_decoder_1_out_40);
  _6x64_Decoder u_6x64_decoder_1 (
    .S0(S0), .S1(S1), .S2(S2), .S3(S3), .S4(S4), .S5(S5), .Out_0(n6x64_decoder_1_out_0),
    .Out_1(n6x64_decoder_1_out_1), .Out_2(n6x64_decoder_1_out_2), .Out_3(n6x64_decoder_1_out_3),
    .Out_4(n6x64_decoder_1_out_4), .Out_7(n6x64_decoder_1_out_7), .Out_8(n6x64_decoder_1_out_8),
    .Out_9(n6x64_decoder_1_out_9), .Out_10(n6x64_decoder_1_out_10), .Out_11(n6x64_decoder_1_out_11),
    .Out_12(n6x64_decoder_1_out_12), .Out_13(n6x64_decoder_1_out_13), .Out_14(n6x64_decoder_1_out_14),
    .Out_17(n6x64_decoder_1_out_17), .Out_18(n6x64_decoder_1_out_18), .Out_19(n6x64_decoder_1_out_19),
    .Out_20(n6x64_decoder_1_out_20), .Out_21(n6x64_decoder_1_out_21), .Out_22(n6x64_decoder_1_out_22),
    .Out_23(n6x64_decoder_1_out_23), .Out_24(n6x64_decoder_1_out_24), .Out_27(n6x64_decoder_1_out_27),
    .Out_28(n6x64_decoder_1_out_28), .Out_29(n6x64_decoder_1_out_29), .Out_30(n6x64_decoder_1_out_30),
    .Out_31(n6x64_decoder_1_out_31), .Out_32(n6x64_decoder_1_out_32), .Out_33(n6x64_decoder_1_out_33),
    .Out_34(n6x64_decoder_1_out_34), .Out_37(n6x64_decoder_1_out_37), .Out_38(n6x64_decoder_1_out_38),
    .Out_39(n6x64_decoder_1_out_39), .Out_40(n6x64_decoder_1_out_40), .Out_41(n6x64_decoder_1_out_41),
    .Out_42(n6x64_decoder_1_out_42), .Out_43(n6x64_decoder_1_out_43), .Out_44(n6x64_decoder_1_out_44),
    .Out_47(n6x64_decoder_1_out_47), .Enable(in_1), .Out_48(n6x64_decoder_1_out_48),
    .Out_49(n6x64_decoder_1_out_49), .Out_50(n6x64_decoder_1_out_50), .Out_51(n6x64_decoder_1_out_51),
    .Out_52(n6x64_decoder_1_out_52), .Out_53(n6x64_decoder_1_out_53), .Out_54(n6x64_decoder_1_out_54),
    .Out_57(n6x64_decoder_1_out_57), .Out_58(n6x64_decoder_1_out_58), .Out_59(n6x64_decoder_1_out_59),
    .Out_60(n6x64_decoder_1_out_60), .Out_62(n6x64_decoder_1_out_62), .Out_63(n6x64_decoder_1_out_63),
    .Out_61(n6x64_decoder_1_out_61));  // open: Out_5, Out_6, Out_15, Out_16, Out_25, Out_26, Out_35, Out_36, Out_45, Out_46, Out_55, Out_56
  or or_4 (or_4_out, n6x64_decoder_1_out_39, n6x64_decoder_1_out_38, n6x64_decoder_1_out_37, n6x64_decoder_1_out_34, n6x64_decoder_1_out_33, n6x64_decoder_1_out_32, n6x64_decoder_1_out_31, n6x64_decoder_1_out_30);
  or or_5 (B, or_1_out, or_2_out, or_3_out, or_4_out, or_6_out, or_7_out, or_8_out);
  or or_6 (or_6_out, n6x64_decoder_1_out_29, n6x64_decoder_1_out_28, n6x64_decoder_1_out_27, n6x64_decoder_1_out_24, n6x64_decoder_1_out_23, n6x64_decoder_1_out_22, n6x64_decoder_1_out_21, n6x64_decoder_1_out_20);
  or or_7 (or_7_out, n6x64_decoder_1_out_19, n6x64_decoder_1_out_18, n6x64_decoder_1_out_17, n6x64_decoder_1_out_14, n6x64_decoder_1_out_13, n6x64_decoder_1_out_12, n6x64_decoder_1_out_11, n6x64_decoder_1_out_10);
  or or_8 (or_8_out, n6x64_decoder_1_out_9, n6x64_decoder_1_out_8, n6x64_decoder_1_out_7, n6x64_decoder_1_out_4, n6x64_decoder_1_out_3, n6x64_decoder_1_out_2, n6x64_decoder_1_out_1, n6x64_decoder_1_out_0);
endmodule

module Segment___C (
  input  in_1,
  input  S5,
  input  S4,
  input  S3,
  input  S2,
  input  S1,
  input  S0,
  output C
);

  wire n6x64_decoder_1_out_0, n6x64_decoder_1_out_1, n6x64_decoder_1_out_3, n6x64_decoder_1_out_4,
       n6x64_decoder_1_out_5, n6x64_decoder_1_out_6, n6x64_decoder_1_out_7, n6x64_decoder_1_out_8,
       n6x64_decoder_1_out_9, n6x64_decoder_1_out_10, n6x64_decoder_1_out_11, n6x64_decoder_1_out_13,
       n6x64_decoder_1_out_14, n6x64_decoder_1_out_15, n6x64_decoder_1_out_16, n6x64_decoder_1_out_17,
       n6x64_decoder_1_out_18, n6x64_decoder_1_out_19, n6x64_decoder_1_out_20, n6x64_decoder_1_out_21,
       n6x64_decoder_1_out_23, n6x64_decoder_1_out_24, n6x64_decoder_1_out_25, n6x64_decoder_1_out_26,
       n6x64_decoder_1_out_27, n6x64_decoder_1_out_28, n6x64_decoder_1_out_29, n6x64_decoder_1_out_30,
       n6x64_decoder_1_out_31, n6x64_decoder_1_out_33, n6x64_decoder_1_out_34, n6x64_decoder_1_out_35,
       n6x64_decoder_1_out_36, n6x64_decoder_1_out_37, n6x64_decoder_1_out_38, n6x64_decoder_1_out_39,
       n6x64_decoder_1_out_40, n6x64_decoder_1_out_41, n6x64_decoder_1_out_43, n6x64_decoder_1_out_44,
       n6x64_decoder_1_out_45, n6x64_decoder_1_out_46, n6x64_decoder_1_out_47, n6x64_decoder_1_out_48,
       n6x64_decoder_1_out_49, n6x64_decoder_1_out_50, n6x64_decoder_1_out_51, n6x64_decoder_1_out_53,
       n6x64_decoder_1_out_54, n6x64_decoder_1_out_55, n6x64_decoder_1_out_56, n6x64_decoder_1_out_57,
       n6x64_decoder_1_out_58, n6x64_decoder_1_out_59, n6x64_decoder_1_out_60, n6x64_decoder_1_out_61,
       n6x64_decoder_1_out_63, or_1_out, or_2_out, or_3_out, or_4_out, or_6_out, or_7_out, or_8_out;

  or or_1 (or_1_out, n6x64_decoder_1_out_63, n6x64_decoder_1_out_61, n6x64_decoder_1_out_60);
  or or_2 (or_2_out, n6x64_decoder_1_out_59, n6x64_decoder_1_out_58, n6x64_decoder_1_out_57, n6x64_decoder_1_out_56, n6x64_decoder_1_out_55, n6x64_decoder_1_out_54, n6x64_decoder_1_out_53, n6x64_decoder_1_out_51, n6x64_decoder_1_out_50);
  or or_3 (or_3_out, n6x64_decoder_1_out_49, n6x64_decoder_1_out_48, n6x64_decoder_1_out_47, n6x64_decoder_1_out_46, n6x64_decoder_1_out_45, n6x64_decoder_1_out_44, n6x64_decoder_1_out_43, n6x64_decoder_1_out_41, n6x64_decoder_1_out_40);
  _6x64_Decoder u_6x64_decoder_1 (
    .S0(S0), .S1(S1), .S2(S2), .S3(S3), .S4(S4), .S5(S5), .Out_0(n6x64_decoder_1_out_0),
    .Out_1(n6x64_decoder_1_out_1), .Out_3(n6x64_decoder_1_out_3), .Out_4(n6x64_decoder_1_out_4),
    .Out_5(n6x64_decoder_1_out_5), .Out_6(n6x64_decoder_1_out_6), .Out_7(n6x64_decoder_1_out_7),
    .Out_8(n6x64_decoder_1_out_8), .Out_9(n6x64_decoder_1_out_9), .Out_10(n6x64_decoder_1_out_10),
    .Out_11(n6x64_decoder_1_out_11), .Out_13(n6x64_decoder_1_out_13), .Out_14(n6x64_decoder_1_out_14),
    .Out_15(n6x64_decoder_1_out_15), .Out_16(n6x64_decoder_1_out_16), .Out_17(n6x64_decoder_1_out_17),
    .Out_18(n6x64_decoder_1_out_18), .Out_19(n6x64_decoder_1_out_19), .Out_20(n6x64_decoder_1_out_20),
    .Out_21(n6x64_decoder_1_out_21), .Out_23(n6x64_decoder_1_out_23), .Out_24(n6x64_decoder_1_out_24),
    .Out_25(n6x64_decoder_1_out_25), .Out_26(n6x64_decoder_1_out_26), .Out_27(n6x64_decoder_1_out_27),
    .Out_28(n6x64_decoder_1_out_28), .Out_29(n6x64_decoder_1_out_29), .Out_30(n6x64_decoder_1_out_30),
    .Out_31(n6x64_decoder_1_out_31), .Out_33(n6x64_decoder_1_out_33), .Out_34(n6x64_decoder_1_out_34),
    .Out_35(n6x64_decoder_1_out_35), .Out_36(n6x64_decoder_1_out_36), .Out_37(n6x64_decoder_1_out_37),
    .Out_38(n6x64_decoder_1_out_38), .Out_39(n6x64_decoder_1_out_39), .Out_40(n6x64_decoder_1_out_40),
    .Out_41(n6x64_decoder_1_out_41), .Out_43(n6x64_decoder_1_out_43), .Out_44(n6x64_decoder_1_out_44),
    .Out_45(n6x64_decoder_1_out_45), .Out_46(n6x64_decoder_1_out_46), .Out_47(n6x64_decoder_1_out_47),
    .Enable(in_1), .Out_48(n6x64_decoder_1_out_48), .Out_49(n6x64_decoder_1_out_49),
    .Out_50(n6x64_decoder_1_out_50), .Out_51(n6x64_decoder_1_out_51), .Out_53(n6x64_decoder_1_out_53),
    .Out_54(n6x64_decoder_1_out_54), .Out_55(n6x64_decoder_1_out_55), .Out_56(n6x64_decoder_1_out_56),
    .Out_57(n6x64_decoder_1_out_57), .Out_58(n6x64_decoder_1_out_58), .Out_59(n6x64_decoder_1_out_59),
    .Out_60(n6x64_decoder_1_out_60), .Out_63(n6x64_decoder_1_out_63), .Out_61(n6x64_decoder_1_out_61));  // open: Out_2, Out_12, Out_22, Out_32, Out_42, Out_52, Out_62
  or or_4 (or_4_out, n6x64_decoder_1_out_39, n6x64_decoder_1_out_38, n6x64_decoder_1_out_37, n6x64_decoder_1_out_36, n6x64_decoder_1_out_35, n6x64_decoder_1_out_34, n6x64_decoder_1_out_33, n6x64_decoder_1_out_31, n6x64_decoder_1_out_30);
  or or_5 (C, or_1_out, or_2_out, or_3_out, or_4_out, or_6_out, or_7_out, or_8_out);
  or or_6 (or_6_out, n6x64_decoder_1_out_29, n6x64_decoder_1_out_28, n6x64_decoder_1_out_27, n6x64_decoder_1_out_26, n6x64_decoder_1_out_25, n6x64_decoder_1_out_24, n6x64_decoder_1_out_23, n6x64_decoder_1_out_21, n6x64_decoder_1_out_20);
  or or_7 (or_7_out, n6x64_decoder_1_out_19, n6x64_decoder_1_out_18, n6x64_decoder_1_out_17, n6x64_decoder_1_out_16, n6x64_decoder_1_out_15, n6x64_decoder_1_out_14, n6x64_decoder_1_out_13, n6x64_decoder_1_out_11, n6x64_decoder_1_out_10);
  or or_8 (or_8_out, n6x64_decoder_1_out_9, n6x64_decoder_1_out_8, n6x64_decoder_1_out_7, n6x64_decoder_1_out_6, n6x64_decoder_1_out_5, n6x64_decoder_1_out_4, n6x64_decoder_1_out_3, n6x64_decoder_1_out_1, n6x64_decoder_1_out_0);
endmodule

module Segment___D (
  input  in_1,
  input  S5,
  input  S4,
  input  S3,
  input  S2,
  input  S1,
  input  S0,
  output D
);

  wire n6x64_decoder_1_out_0, n6x64_decoder_1_out_1, n6x64_decoder_1_out_2, n6x64_decoder_1_out_3,
       n6x64_decoder_1_out_4, n6x64_decoder_1_out_5, n6x64_decoder_1_out_6, n6x64_decoder_1_out_7,
       n6x64_decoder_1_out_8, n6x64_decoder_1_out_9, n6x64_decoder_1_out_10, n6x64_decoder_1_out_11,
       n6x64_decoder_1_out_12, n6x64_decoder_1_out_13, n6x64_decoder_1_out_14, n6x64_decoder_1_out_15,
       n6x64_decoder_1_out_16, n6x64_decoder_1_out_17, n6x64_decoder_1_out_18, n6x64_decoder_1_out_19,
       n6x64_decoder_1_out_20, n6x64_decoder_1_out_21, n6x64_decoder_1_out_22, n6x64_decoder_1_out_23,
       n6x64_decoder_1_out_24, n6x64_decoder_1_out_25, n6x64_decoder_1_out_26, n6x64_decoder_1_out_27,
       n6x64_decoder_1_out_28, n6x64_decoder_1_out_29, n6x64_decoder_1_out_30, n6x64_decoder_1_out_31,
       n6x64_decoder_1_out_32, n6x64_decoder_1_out_33, n6x64_decoder_1_out_34, n6x64_decoder_1_out_35,
       n6x64_decoder_1_out_36, n6x64_decoder_1_out_37, n6x64_decoder_1_out_38, n6x64_decoder_1_out_39,
       n6x64_decoder_1_out_40, n6x64_decoder_1_out_41, n6x64_decoder_1_out_42, n6x64_decoder_1_out_43,
       n6x64_decoder_1_out_44, n6x64_decoder_1_out_45, n6x64_decoder_1_out_46, n6x64_decoder_1_out_47,
       n6x64_decoder_1_out_48, n6x64_decoder_1_out_49, n6x64_decoder_1_out_50, n6x64_decoder_1_out_51,
       n6x64_decoder_1_out_52, n6x64_decoder_1_out_53, n6x64_decoder_1_out_54, n6x64_decoder_1_out_55,
       n6x64_decoder_1_out_56, n6x64_decoder_1_out_57, n6x64_decoder_1_out_58, n6x64_decoder_1_out_59,
       n6x64_decoder_1_out_60, n6x64_decoder_1_out_62, n6x64_decoder_1_out_63, or_1_out, or_2_out, or_3_out,
       or_4_out, or_6_out, or_7_out, or_8_out;

  or or_1 (or_1_out, n6x64_decoder_1_out_63, n6x64_decoder_1_out_62, n6x64_decoder_1_out_60);
  or or_2 (or_2_out, n6x64_decoder_1_out_59, n6x64_decoder_1_out_58, n6x64_decoder_1_out_56, n6x64_decoder_1_out_55, n6x64_decoder_1_out_53, n6x64_decoder_1_out_52, n6x64_decoder_1_out_50);
  or or_3 (or_3_out, n6x64_decoder_1_out_49, n6x64_decoder_1_out_48, n6x64_decoder_1_out_46, n6x64_decoder_1_out_45, n6x64_decoder_1_out_43, n6x64_decoder_1_out_42, n6x64_decoder_1_out_40);
  _6x64_Decoder u_6x64_decoder_1 (
    .S0(S0), .S1(S1), .S2(S2), .S3(S3), .S4(S4), .S5(S5), .Out_0(n6x64_decoder_1_out_0),
    .Out_1(n6x64_decoder_1_out_1), .Out_2(n6x64_decoder_1_out_2), .Out_3(n6x64_decoder_1_out_3),
    .Out_4(n6x64_decoder_1_out_4), .Out_5(n6x64_decoder_1_out_5), .Out_6(n6x64_decoder_1_out_6),
    .Out_7(n6x64_decoder_1_out_7), .Out_8(n6x64_decoder_1_out_8), .Out_9(n6x64_decoder_1_out_9),
    .Out_10(n6x64_decoder_1_out_10), .Out_11(n6x64_decoder_1_out_11), .Out_12(n6x64_decoder_1_out_12),
    .Out_13(n6x64_decoder_1_out_13), .Out_14(n6x64_decoder_1_out_14), .Out_15(n6x64_decoder_1_out_15),
    .Out_16(n6x64_decoder_1_out_16), .Out_17(n6x64_decoder_1_out_17), .Out_18(n6x64_decoder_1_out_18),
    .Out_19(n6x64_decoder_1_out_19), .Out_20(n6x64_decoder_1_out_20), .Out_21(n6x64_decoder_1_out_21),
    .Out_22(n6x64_decoder_1_out_22), .Out_23(n6x64_decoder_1_out_23), .Out_24(n6x64_decoder_1_out_24),
    .Out_25(n6x64_decoder_1_out_25), .Out_26(n6x64_decoder_1_out_26), .Out_27(n6x64_decoder_1_out_27),
    .Out_28(n6x64_decoder_1_out_28), .Out_29(n6x64_decoder_1_out_29), .Out_30(n6x64_decoder_1_out_30),
    .Out_31(n6x64_decoder_1_out_31), .Out_32(n6x64_decoder_1_out_32), .Out_33(n6x64_decoder_1_out_33),
    .Out_34(n6x64_decoder_1_out_34), .Out_35(n6x64_decoder_1_out_35), .Out_36(n6x64_decoder_1_out_36),
    .Out_37(n6x64_decoder_1_out_37), .Out_38(n6x64_decoder_1_out_38), .Out_39(n6x64_decoder_1_out_39),
    .Out_40(n6x64_decoder_1_out_40), .Out_41(n6x64_decoder_1_out_41), .Out_42(n6x64_decoder_1_out_42),
    .Out_43(n6x64_decoder_1_out_43), .Out_44(n6x64_decoder_1_out_44), .Out_45(n6x64_decoder_1_out_45),
    .Out_46(n6x64_decoder_1_out_46), .Out_47(n6x64_decoder_1_out_47), .Enable(in_1),
    .Out_48(n6x64_decoder_1_out_48), .Out_49(n6x64_decoder_1_out_49), .Out_50(n6x64_decoder_1_out_50),
    .Out_51(n6x64_decoder_1_out_51), .Out_52(n6x64_decoder_1_out_52), .Out_53(n6x64_decoder_1_out_53),
    .Out_54(n6x64_decoder_1_out_54), .Out_55(n6x64_decoder_1_out_55), .Out_56(n6x64_decoder_1_out_56),
    .Out_57(n6x64_decoder_1_out_57), .Out_58(n6x64_decoder_1_out_58), .Out_59(n6x64_decoder_1_out_59),
    .Out_60(n6x64_decoder_1_out_60), .Out_62(n6x64_decoder_1_out_62), .Out_63(n6x64_decoder_1_out_63));  // open: Out_61
  or or_4 (or_4_out, n6x64_decoder_1_out_39, n6x64_decoder_1_out_38, n6x64_decoder_1_out_36, n6x64_decoder_1_out_35, n6x64_decoder_1_out_33, n6x64_decoder_1_out_32, n6x64_decoder_1_out_30);
  or or_5 (D, or_1_out, or_2_out, or_3_out, or_4_out, or_6_out, or_7_out, or_8_out);
  or or_6 (or_6_out, n6x64_decoder_1_out_29, n6x64_decoder_1_out_28, n6x64_decoder_1_out_26, n6x64_decoder_1_out_25, n6x64_decoder_1_out_23, n6x64_decoder_1_out_22, n6x64_decoder_1_out_20);
  or or_7 (or_7_out, n6x64_decoder_1_out_19, n6x64_decoder_1_out_18, n6x64_decoder_1_out_16, n6x64_decoder_1_out_15, n6x64_decoder_1_out_13, n6x64_decoder_1_out_12, n6x64_decoder_1_out_10);
  or or_8 (or_8_out, n6x64_decoder_1_out_9, n6x64_decoder_1_out_8, n6x64_decoder_1_out_6, n6x64_decoder_1_out_5, n6x64_decoder_1_out_3, n6x64_decoder_1_out_2, n6x64_decoder_1_out_0);
endmodule

module Segment___E (
  input  in_1,
  input  S5,
  input  S4,
  input  S3,
  input  S2,
  input  S1,
  input  S0,
  output D
);

  wire n6x64_decoder_1_out_0, n6x64_decoder_1_out_2, n6x64_decoder_1_out_6, n6x64_decoder_1_out_8,
       n6x64_decoder_1_out_10, n6x64_decoder_1_out_12, n6x64_decoder_1_out_16, n6x64_decoder_1_out_18,
       n6x64_decoder_1_out_20, n6x64_decoder_1_out_22, n6x64_decoder_1_out_26, n6x64_decoder_1_out_28,
       n6x64_decoder_1_out_30, n6x64_decoder_1_out_32, n6x64_decoder_1_out_36, n6x64_decoder_1_out_38,
       n6x64_decoder_1_out_40, n6x64_decoder_1_out_42, n6x64_decoder_1_out_46, n6x64_decoder_1_out_48,
       n6x64_decoder_1_out_50, n6x64_decoder_1_out_52, n6x64_decoder_1_out_56, n6x64_decoder_1_out_58,
       n6x64_decoder_1_out_60, n6x64_decoder_1_out_62, or_1_out, or_2_out, or_3_out, or_4_out, or_6_out,
       or_7_out, or_8_out;

  or or_1 (or_1_out, n6x64_decoder_1_out_62, n6x64_decoder_1_out_60);
  or or_2 (or_2_out, n6x64_decoder_1_out_58, n6x64_decoder_1_out_56, n6x64_decoder_1_out_52, n6x64_decoder_1_out_50);
  or or_3 (or_3_out, n6x64_decoder_1_out_48, n6x64_decoder_1_out_46, n6x64_decoder_1_out_42, n6x64_decoder_1_out_40);
  _6x64_Decoder u_6x64_decoder_1 (
    .S0(S0), .S1(S1), .S2(S2), .S3(S3), .S4(S4), .S5(S5), .Out_0(n6x64_decoder_1_out_0),
    .Out_2(n6x64_decoder_1_out_2), .Out_6(n6x64_decoder_1_out_6), .Out_8(n6x64_decoder_1_out_8),
    .Out_10(n6x64_decoder_1_out_10), .Out_12(n6x64_decoder_1_out_12), .Out_16(n6x64_decoder_1_out_16),
    .Out_18(n6x64_decoder_1_out_18), .Out_20(n6x64_decoder_1_out_20), .Out_22(n6x64_decoder_1_out_22),
    .Out_26(n6x64_decoder_1_out_26), .Out_28(n6x64_decoder_1_out_28), .Out_30(n6x64_decoder_1_out_30),
    .Out_32(n6x64_decoder_1_out_32), .Out_36(n6x64_decoder_1_out_36), .Out_38(n6x64_decoder_1_out_38),
    .Out_40(n6x64_decoder_1_out_40), .Out_42(n6x64_decoder_1_out_42), .Out_46(n6x64_decoder_1_out_46),
    .Enable(in_1), .Out_48(n6x64_decoder_1_out_48), .Out_50(n6x64_decoder_1_out_50),
    .Out_52(n6x64_decoder_1_out_52), .Out_56(n6x64_decoder_1_out_56), .Out_58(n6x64_decoder_1_out_58),
    .Out_60(n6x64_decoder_1_out_60), .Out_62(n6x64_decoder_1_out_62));  // open: Out_1, Out_3, Out_4, Out_5, Out_7, Out_9, Out_11, Out_13, Out_14, Out_15, Out_17, Out_19, Out_21, Out_23, Out_24, Out_25, Out_27, Out_29, Out_31, Out_33, Out_34, Out_35, Out_37, Out_39, Out_41, Out_43, Out_44, Out_45, Out_47, Out_49, Out_51, Out_53, Out_54, Out_55, Out_57, Out_59, Out_63, Out_61
  or or_4 (or_4_out, n6x64_decoder_1_out_38, n6x64_decoder_1_out_36, n6x64_decoder_1_out_32, n6x64_decoder_1_out_30);
  or or_5 (D, or_1_out, or_2_out, or_3_out, or_4_out, or_6_out, or_7_out, or_8_out);
  or or_6 (or_6_out, n6x64_decoder_1_out_28, n6x64_decoder_1_out_26, n6x64_decoder_1_out_22, n6x64_decoder_1_out_20);
  or or_7 (or_7_out, n6x64_decoder_1_out_18, n6x64_decoder_1_out_16, n6x64_decoder_1_out_12, n6x64_decoder_1_out_10);
  or or_8 (or_8_out, n6x64_decoder_1_out_8, n6x64_decoder_1_out_6, n6x64_decoder_1_out_2, n6x64_decoder_1_out_0);
endmodule

module Segment___F (
  input  in_1,
  input  S5,
  input  S4,
  input  S3,
  input  S2,
  input  S1,
  input  S0,
  output F
);

  wire n6x64_decoder_1_out_0, n6x64_decoder_1_out_4, n6x64_decoder_1_out_5, n6x64_decoder_1_out_6,
       n6x64_decoder_1_out_8, n6x64_decoder_1_out_9, n6x64_decoder_1_out_10, n6x64_decoder_1_out_14,
       n6x64_decoder_1_out_15, n6x64_decoder_1_out_16, n6x64_decoder_1_out_18, n6x64_decoder_1_out_19,
       n6x64_decoder_1_out_20, n6x64_decoder_1_out_24, n6x64_decoder_1_out_25, n6x64_decoder_1_out_26,
       n6x64_decoder_1_out_28, n6x64_decoder_1_out_29, n6x64_decoder_1_out_30, n6x64_decoder_1_out_34,
       n6x64_decoder_1_out_35, n6x64_decoder_1_out_36, n6x64_decoder_1_out_38, n6x64_decoder_1_out_39,
       n6x64_decoder_1_out_40, n6x64_decoder_1_out_44, n6x64_decoder_1_out_45, n6x64_decoder_1_out_46,
       n6x64_decoder_1_out_48, n6x64_decoder_1_out_49, n6x64_decoder_1_out_50, n6x64_decoder_1_out_54,
       n6x64_decoder_1_out_55, n6x64_decoder_1_out_56, n6x64_decoder_1_out_58, n6x64_decoder_1_out_59,
       n6x64_decoder_1_out_60, or_1_out, or_2_out, or_3_out, or_5_out, or_6_out, or_7_out;

  or or_1 (or_1_out, n6x64_decoder_1_out_60, n6x64_decoder_1_out_59, n6x64_decoder_1_out_58, n6x64_decoder_1_out_56, n6x64_decoder_1_out_55, n6x64_decoder_1_out_54, n6x64_decoder_1_out_50);
  or or_2 (or_2_out, n6x64_decoder_1_out_49, n6x64_decoder_1_out_48, n6x64_decoder_1_out_46, n6x64_decoder_1_out_45, n6x64_decoder_1_out_44, n6x64_decoder_1_out_40);
  _6x64_Decoder u_6x64_decoder_1 (
    .S0(S0), .S1(S1), .S2(S2), .S3(S3), .S4(S4), .S5(S5), .Out_0(n6x64_decoder_1_out_0),
    .Out_4(n6x64_decoder_1_out_4), .Out_5(n6x64_decoder_1_out_5), .Out_6(n6x64_decoder_1_out_6),
    .Out_8(n6x64_decoder_1_out_8), .Out_9(n6x64_decoder_1_out_9), .Out_10(n6x64_decoder_1_out_10),
    .Out_14(n6x64_decoder_1_out_14), .Out_15(n6x64_decoder_1_out_15), .Out_16(n6x64_decoder_1_out_16),
    .Out_18(n6x64_decoder_1_out_18), .Out_19(n6x64_decoder_1_out_19), .Out_20(n6x64_decoder_1_out_20),
    .Out_24(n6x64_decoder_1_out_24), .Out_25(n6x64_decoder_1_out_25), .Out_26(n6x64_decoder_1_out_26),
    .Out_28(n6x64_decoder_1_out_28), .Out_29(n6x64_decoder_1_out_29), .Out_30(n6x64_decoder_1_out_30),
    .Out_34(n6x64_decoder_1_out_34), .Out_35(n6x64_decoder_1_out_35), .Out_36(n6x64_decoder_1_out_36),
    .Out_38(n6x64_decoder_1_out_38), .Out_39(n6x64_decoder_1_out_39), .Out_40(n6x64_decoder_1_out_40),
    .Out_44(n6x64_decoder_1_out_44), .Out_45(n6x64_decoder_1_out_45), .Out_46(n6x64_decoder_1_out_46),
    .Enable(in_1), .Out_48(n6x64_decoder_1_out_48), .Out_49(n6x64_decoder_1_out_49),
    .Out_50(n6x64_decoder_1_out_50), .Out_54(n6x64_decoder_1_out_54), .Out_55(n6x64_decoder_1_out_55),
    .Out_56(n6x64_decoder_1_out_56), .Out_58(n6x64_decoder_1_out_58), .Out_59(n6x64_decoder_1_out_59),
    .Out_60(n6x64_decoder_1_out_60));  // open: Out_1, Out_2, Out_3, Out_7, Out_11, Out_12, Out_13, Out_17, Out_21, Out_22, Out_23, Out_27, Out_31, Out_32, Out_33, Out_37, Out_41, Out_42, Out_43, Out_47, Out_51, Out_52, Out_53, Out_57, Out_62, Out_63, Out_61
  or or_3 (or_3_out, n6x64_decoder_1_out_39, n6x64_decoder_1_out_38, n6x64_decoder_1_out_36, n6x64_decoder_1_out_35, n6x64_decoder_1_out_34, n6x64_decoder_1_out_30);
  or or_4 (F, or_1_out, or_2_out, or_3_out, or_5_out, or_6_out, or_7_out);
  or or_5 (or_5_out, n6x64_decoder_1_out_29, n6x64_decoder_1_out_28, n6x64_decoder_1_out_26, n6x64_decoder_1_out_25, n6x64_decoder_1_out_24, n6x64_decoder_1_out_20);
  or or_6 (or_6_out, n6x64_decoder_1_out_19, n6x64_decoder_1_out_18, n6x64_decoder_1_out_16, n6x64_decoder_1_out_15, n6x64_decoder_1_out_14, n6x64_decoder_1_out_10);
  or or_7 (or_7_out, n6x64_decoder_1_out_9, n6x64_decoder_1_out_8, n6x64_decoder_1_out_6, n6x64_decoder_1_out_5, n6x64_decoder_1_out_4, n6x64_decoder_1_out_0);
endmodule

module Segment___G (
  input  in_1,
  input  S5,
  input  S4,
  input  S3,
  input  S2,
  input  S1,
  input  S0,
  output G
);

  wire n6x64_decoder_1_out_2, n6x64_decoder_1_out_3, n6x64_decoder_1_out_4, n6x64_decoder_1_out_5,
       n6x64_decoder_1_out_6, n6x64_decoder_1_out_8, n6x64_decoder_1_out_9, n6x64_decoder_1_out_12,
       n6x64_decoder_1_out_13, n6x64_decoder_1_out_14, n6x64_decoder_1_out_15, n6x64_decoder_1_out_16,
       n6x64_decoder_1_out_18, n6x64_decoder_1_out_19, n6x64_decoder_1_out_22, n6x64_decoder_1_out_23,
       n6x64_decoder_1_out_24, n6x64_decoder_1_out_25, n6x64_decoder_1_out_26, n6x64_decoder_1_out_28,
       n6x64_decoder_1_out_29, n6x64_decoder_1_out_32, n6x64_decoder_1_out_33, n6x64_decoder_1_out_34,
       n6x64_decoder_1_out_35, n6x64_decoder_1_out_36, n6x64_decoder_1_out_38, n6x64_decoder_1_out_39,
       n6x64_decoder_1_out_42, n6x64_decoder_1_out_43, n6x64_decoder_1_out_44, n6x64_decoder_1_out_45,
       n6x64_decoder_1_out_46, n6x64_decoder_1_out_48, n6x64_decoder_1_out_49, n6x64_decoder_1_out_52,
       n6x64_decoder_1_out_53, n6x64_decoder_1_out_54, n6x64_decoder_1_out_55, n6x64_decoder_1_out_56,
       n6x64_decoder_1_out_58, n6x64_decoder_1_out_59, n6x64_decoder_1_out_62, n6x64_decoder_1_out_63,
       or_1_out, or_2_out, or_3_out, or_4_out, or_6_out, or_7_out, or_8_out;

  or or_1 (or_1_out, n6x64_decoder_1_out_63, n6x64_decoder_1_out_62);
  or or_2 (or_2_out, n6x64_decoder_1_out_59, n6x64_decoder_1_out_58, n6x64_decoder_1_out_56, n6x64_decoder_1_out_55, n6x64_decoder_1_out_54, n6x64_decoder_1_out_53, n6x64_decoder_1_out_52);
  or or_3 (or_3_out, n6x64_decoder_1_out_49, n6x64_decoder_1_out_48, n6x64_decoder_1_out_46, n6x64_decoder_1_out_45, n6x64_decoder_1_out_44, n6x64_decoder_1_out_43, n6x64_decoder_1_out_42);
  _6x64_Decoder u_6x64_decoder_1 (
    .S0(S0), .S1(S1), .S2(S2), .S3(S3), .S4(S4), .S5(S5), .Out_2(n6x64_decoder_1_out_2),
    .Out_3(n6x64_decoder_1_out_3), .Out_4(n6x64_decoder_1_out_4), .Out_5(n6x64_decoder_1_out_5),
    .Out_6(n6x64_decoder_1_out_6), .Out_8(n6x64_decoder_1_out_8), .Out_9(n6x64_decoder_1_out_9),
    .Out_12(n6x64_decoder_1_out_12), .Out_13(n6x64_decoder_1_out_13), .Out_14(n6x64_decoder_1_out_14),
    .Out_15(n6x64_decoder_1_out_15), .Out_16(n6x64_decoder_1_out_16), .Out_18(n6x64_decoder_1_out_18),
    .Out_19(n6x64_decoder_1_out_19), .Out_22(n6x64_decoder_1_out_22), .Out_23(n6x64_decoder_1_out_23),
    .Out_24(n6x64_decoder_1_out_24), .Out_25(n6x64_decoder_1_out_25), .Out_26(n6x64_decoder_1_out_26),
    .Out_28(n6x64_decoder_1_out_28), .Out_29(n6x64_decoder_1_out_29), .Out_32(n6x64_decoder_1_out_32),
    .Out_33(n6x64_decoder_1_out_33), .Out_34(n6x64_decoder_1_out_34), .Out_35(n6x64_decoder_1_out_35),
    .Out_36(n6x64_decoder_1_out_36), .Out_38(n6x64_decoder_1_out_38), .Out_39(n6x64_decoder_1_out_39),
    .Out_42(n6x64_decoder_1_out_42), .Out_43(n6x64_decoder_1_out_43), .Out_44(n6x64_decoder_1_out_44),
    .Out_45(n6x64_decoder_1_out_45), .Out_46(n6x64_decoder_1_out_46), .Enable(in_1),
    .Out_48(n6x64_decoder_1_out_48), .Out_49(n6x64_decoder_1_out_49), .Out_52(n6x64_decoder_1_out_52),
    .Out_53(n6x64_decoder_1_out_53), .Out_54(n6x64_decoder_1_out_54), .Out_55(n6x64_decoder_1_out_55),
    .Out_56(n6x64_decoder_1_out_56), .Out_58(n6x64_decoder_1_out_58), .Out_59(n6x64_decoder_1_out_59),
    .Out_62(n6x64_decoder_1_out_62), .Out_63(n6x64_decoder_1_out_63));  // open: Out_0, Out_1, Out_7, Out_10, Out_11, Out_17, Out_20, Out_21, Out_27, Out_30, Out_31, Out_37, Out_40, Out_41, Out_47, Out_50, Out_51, Out_57, Out_60, Out_61
  or or_4 (or_4_out, n6x64_decoder_1_out_39, n6x64_decoder_1_out_38, n6x64_decoder_1_out_36, n6x64_decoder_1_out_35, n6x64_decoder_1_out_34, n6x64_decoder_1_out_33, n6x64_decoder_1_out_32);
  or or_5 (G, or_1_out, or_2_out, or_3_out, or_4_out, or_6_out, or_7_out, or_8_out);
  or or_6 (or_6_out, n6x64_decoder_1_out_29, n6x64_decoder_1_out_28, n6x64_decoder_1_out_26, n6x64_decoder_1_out_25, n6x64_decoder_1_out_24, n6x64_decoder_1_out_23, n6x64_decoder_1_out_22);
  or or_7 (or_7_out, n6x64_decoder_1_out_19, n6x64_decoder_1_out_18, n6x64_decoder_1_out_16, n6x64_decoder_1_out_15, n6x64_decoder_1_out_14, n6x64_decoder_1_out_13, n6x64_decoder_1_out_12);
  or or_8 (or_8_out, n6x64_decoder_1_out_9, n6x64_decoder_1_out_8, n6x64_decoder_1_out_6, n6x64_decoder_1_out_5, n6x64_decoder_1_out_4, n6x64_decoder_1_out_3, n6x64_decoder_1_out_2);
endmodule

module Get_Segment_carry (
  input  in_1,
  input  S5,
  input  S4,
  input  S3,
  input  S2,
  input  S1,
  input  S0,
  output Six,
  output Five,
  output Four,
  output Three,
  output Two,
  output One
);

  wire n6x64_decoder_1_out_10, n6x64_decoder_1_out_11, n6x64_decoder_1_out_12, n6x64_decoder_1_out_13,
       n6x64_decoder_1_out_14, n6x64_decoder_1_out_15, n6x64_decoder_1_out_16, n6x64_decoder_1_out_17,
       n6x64_decoder_1_out_18, n6x64_decoder_1_out_19, n6x64_decoder_1_out_20, n6x64_decoder_1_out_21,
       n6x64_decoder_1_out_22, n6x64_decoder_1_out_23, n6x64_decoder_1_out_24, n6x64_decoder_1_out_25,
       n6x64_decoder_1_out_26, n6x64_decoder_1_out_27, n6x64_decoder_1_out_28, n6x64_decoder_1_out_29,
       n6x64_decoder_1_out_30, n6x64_decoder_1_out_31, n6x64_decoder_1_out_32, n6x64_decoder_1_out_33,
       n6x64_decoder_1_out_34, n6x64_decoder_1_out_35, n6x64_decoder_1_out_36, n6x64_decoder_1_out_37,
       n6x64_decoder_1_out_38, n6x64_decoder_1_out_39, n6x64_decoder_1_out_40, n6x64_decoder_1_out_41,
       n6x64_decoder_1_out_42, n6x64_decoder_1_out_43, n6x64_decoder_1_out_44, n6x64_decoder_1_out_45,
       n6x64_decoder_1_out_46, n6x64_decoder_1_out_47, n6x64_decoder_1_out_48, n6x64_decoder_1_out_49,
       n6x64_decoder_1_out_50, n6x64_decoder_1_out_51, n6x64_decoder_1_out_52, n6x64_decoder_1_out_53,
       n6x64_decoder_1_out_54, n6x64_decoder_1_out_55, n6x64_decoder_1_out_56, n6x64_decoder_1_out_57,
       n6x64_decoder_1_out_58, n6x64_decoder_1_out_59, n6x64_decoder_1_out_60, n6x64_decoder_1_out_61,
       n6x64_decoder_1_out_62, n6x64_decoder_1_out_63;

  or or_1 (Six, n6x64_decoder_1_out_63, n6x64_decoder_1_out_62, n6x64_decoder_1_out_61, n6x64_decoder_1_out_60);
  or or_2 (Five, n6x64_decoder_1_out_59, n6x64_decoder_1_out_58, n6x64_decoder_1_out_57, n6x64_decoder_1_out_56, n6x64_decoder_1_out_55, n6x64_decoder_1_out_54, n6x64_decoder_1_out_53, n6x64_decoder_1_out_52, n6x64_decoder_1_out_51, n6x64_decoder_1_out_50);
  or or_3 (Four, n6x64_decoder_1_out_49, n6x64_decoder_1_out_48, n6x64_decoder_1_out_47, n6x64_decoder_1_out_46, n6x64_decoder_1_out_45, n6x64_decoder_1_out_44, n6x64_decoder_1_out_43, n6x64_decoder_1_out_42, n6x64_decoder_1_out_41, n6x64_decoder_1_out_40);
  _6x64_Decoder u_6x64_decoder_1 (
    .S0(S0), .S1(S1), .S2(S2), .S3(S3), .S4(S4), .S5(S5), .Out_10(n6x64_decoder_1_out_10),
    .Out_11(n6x64_decoder_1_out_11), .Out_12(n6x64_decoder_1_out_12), .Out_13(n6x64_decoder_1_out_13),
    .Out_14(n6x64_decoder_1_out_14), .Out_15(n6x64_decoder_1_out_15), .Out_16(n6x64_decoder_1_out_16),
    .Out_17(n6x64_decoder_1_out_17), .Out_18(n6x64_decoder_1_out_18), .Out_19(n6x64_decoder_1_out_19),
    .Out_20(n6x64_decoder_1_out_20), .Out_21(n6x64_decoder_1_out_21), .Out_22(n6x64_decoder_1_out_22),
    .Out_23(n6x64_decoder_1_out_23), .Out_24(n6x64_decoder_1_out_24), .Out_25(n6x64_decoder_1_out_25),
    .Out_26(n6x64_decoder_1_out_26), .Out_27(n6x64_decoder_1_out_27), .Out_28(n6x64_decoder_1_out_28),
    .Out_29(n6x64_decoder_1_out_29), .Out_30(n6x64_decoder_1_out_30), .Out_31(n6x64_decoder_1_out_31),
    .Out_32(n6x64_decoder_1_out_32), .Out_33(n6x64_decoder_1_out_33), .Out_34(n6x64_decoder_1_out_34),
    .Out_35(n6x64_decoder_1_out_35), .Out_36(n6x64_decoder_1_out_36), .Out_37(n6x64_decoder_1_out_37),
    .Out_38(n6x64_decoder_1_out_38), .Out_39(n6x64_decoder_1_out_39), .Out_40(n6x64_decoder_1_out_40),
    .Out_41(n6x64_decoder_1_out_41), .Out_42(n6x64_decoder_1_out_42), .Out_43(n6x64_decoder_1_out_43),
    .Out_44(n6x64_decoder_1_out_44), .Out_45(n6x64_decoder_1_out_45), .Out_46(n6x64_decoder_1_out_46),
    .Out_47(n6x64_decoder_1_out_47), .Enable(in_1), .Out_48(n6x64_decoder_1_out_48),
    .Out_49(n6x64_decoder_1_out_49), .Out_50(n6x64_decoder_1_out_50), .Out_51(n6x64_decoder_1_out_51),
    .Out_52(n6x64_decoder_1_out_52), .Out_53(n6x64_decoder_1_out_53), .Out_54(n6x64_decoder_1_out_54),
    .Out_55(n6x64_decoder_1_out_55), .Out_56(n6x64_decoder_1_out_56), .Out_57(n6x64_decoder_1_out_57),
    .Out_58(n6x64_decoder_1_out_58), .Out_59(n6x64_decoder_1_out_59), .Out_60(n6x64_decoder_1_out_60),
    .Out_62(n6x64_decoder_1_out_62), .Out_63(n6x64_decoder_1_out_63), .Out_61(n6x64_decoder_1_out_61));  // open: Out_0, Out_1, Out_2, Out_3, Out_4, Out_5, Out_6, Out_7, Out_8, Out_9
  or or_4 (Three, n6x64_decoder_1_out_39, n6x64_decoder_1_out_38, n6x64_decoder_1_out_37, n6x64_decoder_1_out_36, n6x64_decoder_1_out_35, n6x64_decoder_1_out_34, n6x64_decoder_1_out_33, n6x64_decoder_1_out_32, n6x64_decoder_1_out_31, n6x64_decoder_1_out_30);
  or or_5 (Two, n6x64_decoder_1_out_29, n6x64_decoder_1_out_28, n6x64_decoder_1_out_27, n6x64_decoder_1_out_26, n6x64_decoder_1_out_25, n6x64_decoder_1_out_24, n6x64_decoder_1_out_23, n6x64_decoder_1_out_22, n6x64_decoder_1_out_21, n6x64_decoder_1_out_20);
  or or_6 (One, n6x64_decoder_1_out_19, n6x64_decoder_1_out_18, n6x64_decoder_1_out_17, n6x64_decoder_1_out_16, n6x64_decoder_1_out_15, n6x64_decoder_1_out_14, n6x64_decoder_1_out_13, n6x64_decoder_1_out_12, n6x64_decoder_1_out_11, n6x64_decoder_1_out_10);
endmodule

module Display_Carry (
  input  Six,
  input  Five,
  input  Four,
  input  Three,
  input  Two,
  input  One,
  output A,
  output B,
  output C,
  output D,
  output E,
  output F,
  output G
);

  or u_A (A, Two, Three, Five, Six);
  or u_B (B, One, Two, Three, Four);
  or u_C (C, One, Three, Four, Five, Six);
  or u_D (D, Two, Three, Five, Six);
  or u_E (E, Two, Six);
  or u_F (F, Four, Five, Six);
  or u_G (G, Two, Three, Four, Five, Six);
endmodule

module Display_Hex (
  input  _32,
  input  _16,
  input  _8,
  input  _4,
  input  _2,
  input  _1,
  input  switsh,
  output [3:0] out_8,
  output [3:0] out_9
);

  and and_1 (out_8[1], switsh, _32);
  and and_2 (out_8[0], switsh, _16);
  and and_3 (out_9[3], switsh, _8);
  and and_4 (out_9[2], switsh, _4);
  and and_5 (out_9[1], switsh, _2);
  and and_6 (out_9[0], switsh, _1);

  assign out_8[3:2] = 2'b00;
endmodule
